// Logisim project ALU_MPS_ASSIGNMENT.circ as structural Verilog: 3 circuits, main circuit main
module main (
);

  ALU alu_1 ();  // open: reg1, reg2, opcode, ALUout
endmodule

module ALU (
  input  [3:0] reg1,
  input  [3:0] reg2,
  input  [1:0] opcode,
  output [3:0] ALUout
);

  wire [3:0] adder_1_out, adder_2_out, subtractor_1_out, subtractor_2_out;

  Adder #(.width(4)) adder_1 (.a(reg1), .b(reg2), .out(adder_1_out));  // open: cin, cout
  Subtractor #(.width(4)) subtractor_1 (.a(reg1), .b(reg2), .out(subtractor_1_out));  // open: bin, bout
  Adder #(.width(4)) adder_2 (.a(reg1), .b(4'b0001), .out(adder_2_out));  // open: cin, cout
  Subtractor #(.width(4)) subtractor_2 (.a(reg1), .b(4'b0001), .out(subtractor_2_out));  // open: bin, bout
  Multiplexer #(.select(2), .width(4)) multiplexer_1 (
    .in0(adder_1_out), .in1(subtractor_1_out), .in2(adder_2_out), .in3(subtractor_2_out), .out(ALUout),
    .sel(opcode));
endmodule

module ALUtest (
  input  [3:0] FromReg_1,
  input  [3:0] FromReg_2,
  input  [1:0] SplitOp
);

  wire [3:0] adder_1_out, multiplexer_1_out, negator_1_out, negator_2_out, subtractor_1_out;

  Adder #(.width(4)) adder_1 (.a(FromReg_1), .b(FromReg_2), .out(adder_1_out));  // open: cin, cout
  Subtractor #(.width(4)) subtractor_1 (.a(FromReg_1), .b(FromReg_2), .out(subtractor_1_out));  // open: bin, bout
  Negator #(.width(4)) negator_1 (.in(FromReg_1), .out(negator_1_out));
  Negator #(.width(4)) negator_2 (.in(FromReg_2), .out(negator_2_out));
  Multiplexer #(.select(2), .width(4)) multiplexer_1 (
    .in0(adder_1_out), .in1(subtractor_1_out), .in2(negator_1_out), .in3(negator_2_out),
    .out(multiplexer_1_out), .sel(SplitOp));
  // Probe on multiplexer_1_out
endmodule
