// Logisim project DataPath.circ as structural Verilog: 5 circuits, main circuit main
module main (
  input  in_1
);

  wire clock_1_out, comparator_1_gt;
  wire [1:0] multiplexer_1_out, rom_1_data_2;
  wire [3:0] adder_1_out, alu_1_aluout, multiplexer_2_out, register_1_q, rf_1_readdata_1, rf_1_readdata_2;
  wire [7:0] rom_1_data;

  Clock clock_1 (.out(clock_1_out));
  Register #(.width(4)) register_1 (.D(adder_1_out), .en(in_1), .Q(register_1_q), .clk(clock_1_out));  // open: clr
  // Probe on rom_1_data[4:3]
  Multiplexer #(.width(2)) multiplexer_1 (
    .in0(rom_1_data_2), .in1(rom_1_data_2), .out(multiplexer_1_out), .sel(comparator_1_gt));
  // Probe on rom_1_data_2
  Adder #(.width(4)) adder_1 (.a(register_1_q), .b(4'b0001), .out(adder_1_out));  // open: cin, cout
  ROM #(.addrWidth(4)) rom_1 (.addr(register_1_q), .data({rom_1_data[7:3], rom_1_data_2, rom_1_data[0]}));
  // Probe on rf_1_readdata_1
  // Probe on rf_1_readdata_2
  RF rf_1 (
    .ReadReg_1(rom_1_data_2), .ReadReg_2(rom_1_data[4:3]), .CLK_enable(clock_1_out),
    .Write_data(multiplexer_2_out), .select_reg_pin(multiplexer_1_out), .ReadData_1(rf_1_readdata_1),
    .ReadData_2(rf_1_readdata_2));
  // Probe on {rom_1_data[7:3], rom_1_data_2, rom_1_data[0]}
  ALU alu_1 (
    .reg1(rf_1_readdata_1), .reg2(rf_1_readdata_2), .opcode(rom_1_data[6:5]), .ALUout(alu_1_aluout));  // open: zeroout, zeroo
  // Probe on rom_1_data[6:5]
  // Probe on rom_1_data[7:5]
  // Probe on {rom_1_data[4:3], rom_1_data_2}
  // Probe on alu_1_aluout
  // Probe on multiplexer_2_out
  // Probe on comparator_1_gt
  Comparator #(.width(3)) comparator_1 (.a(rom_1_data[7:5]), .b(3'b101), .gt(comparator_1_gt));  // open: eq, lt
  Multiplexer #(.width(4)) multiplexer_2 (
    .in0({rom_1_data[4:3], rom_1_data_2}), .in1(alu_1_aluout), .out(multiplexer_2_out), .sel(comparator_1_gt));

  // Notes on the sheet:
  //   contents of rom_1 (hex, n*v repeats v):
  //   a8 a2 ac a6 2 32 47 66
endmodule

module ALU (
  input  [3:0] zeroout,
  input  [3:0] reg1,
  input  [3:0] reg2,
  input  [1:0] opcode,
  output [3:0] zeroo,
  output [3:0] ALUout
);

  wire [3:0] adder_1_out, negator_1_out, negator_2_out, subtractor_1_out;

  Adder #(.width(4)) adder_1 (.a(reg1), .b(reg2), .out(adder_1_out));  // open: cin, cout
  Subtractor #(.width(4)) subtractor_1 (.a(reg1), .b(reg2), .out(subtractor_1_out));  // open: bin, bout
  Negator #(.width(4)) negator_1 (.in(reg1), .out(negator_1_out));
  Negator #(.width(4)) negator_2 (.in(reg2), .out(negator_2_out));
  Comparator comparator_1 ();  // open: a, b, gt, eq, lt
  Multiplexer #(.select(2), .width(4)) multiplexer_1 (
    .in0(adder_1_out), .in1(subtractor_1_out), .in2(negator_1_out), .in3(negator_2_out), .out(ALUout),
    .sel(opcode));

  assign zeroo = zeroout;
endmodule

module RF (
  input  [1:0] ReadReg_1,
  input  [1:0] ReadReg_2,
  input  CLK_enable,
  input  [3:0] Write_data,
  input  [1:0] select_reg_pin,
  output [3:0] ReadData_1,
  output [3:0] ReadData_2
);

  wire and_1_out, and_2_out, and_3_out, and_4_out, decoder_1_out0, decoder_1_out1, decoder_1_out2,
       decoder_1_out3;
  wire [3:0] register_1_q, register_2_q, register_3_q, register_4_q;

  and and_1 (and_1_out, CLK_enable, decoder_1_out0);
  and and_2 (and_2_out, CLK_enable, decoder_1_out1);
  and and_3 (and_3_out, CLK_enable, decoder_1_out2);
  and and_4 (and_4_out, CLK_enable, decoder_1_out3);
  Register #(.width(4)) register_1 (.D(Write_data), .Q(register_1_q), .clk(and_1_out));  // open: en, clr
  Register #(.width(4)) register_2 (.D(Write_data), .Q(register_2_q), .clk(and_2_out));  // open: en, clr
  Register #(.width(4)) register_3 (.D(Write_data), .Q(register_3_q), .clk(and_3_out));  // open: en, clr
  Register #(.width(4)) register_4 (.D(Write_data), .Q(register_4_q), .clk(and_4_out));  // open: en, clr
  Decoder #(.select(2)) decoder_1 (
    .out0(decoder_1_out0), .out1(decoder_1_out1), .out2(decoder_1_out2), .out3(decoder_1_out3),
    .sel(select_reg_pin), .en(CLK_enable));
  Multiplexer #(.select(2), .width(4)) multiplexer_1 (
    .in0(register_1_q), .in1(register_2_q), .in2(register_3_q), .in3(register_4_q), .out(ReadData_1),
    .sel(ReadReg_1));
  Multiplexer #(.select(2), .width(4)) multiplexer_2 (
    .in0(register_1_q), .in1(register_2_q), .in2(register_3_q), .in3(register_4_q), .out(ReadData_2),
    .sel(ReadReg_2));
endmodule

module RFtest (
  input  [1:0] ReadReg_1,
  input  [1:0] ReadReg_2,
  input  Write_enable,
  input  [3:0] WriteData,
  input  in_5,
  input  [1:0] select_reg,
  output [3:0] ReadData_1,
  output [3:0] ReadData_2
);

  wire and_1_out, and_2_out, and_3_out, and_4_out, decoder_1_out0, decoder_1_out1, decoder_1_out2,
       decoder_1_out3;
  wire [3:0] register_1_q, register_2_q, register_3_q, register_4_q;

  and and_1 (and_1_out, Write_enable, decoder_1_out0);
  and and_2 (and_2_out, Write_enable, decoder_1_out1);
  and and_3 (and_3_out, Write_enable, decoder_1_out2);
  and and_4 (and_4_out, Write_enable, decoder_1_out3);
  Register #(.width(4)) register_1 (.D(WriteData), .Q(register_1_q), .clk(and_1_out));  // open: en, clr
  Register #(.width(4)) register_2 (.D(WriteData), .Q(register_2_q), .clk(and_2_out));  // open: en, clr
  Register #(.width(4)) register_3 (.D(WriteData), .Q(register_3_q), .clk(and_3_out));  // open: en, clr
  Register #(.width(4)) register_4 (.D(WriteData), .Q(register_4_q), .clk(and_4_out));  // open: en, clr
  Decoder #(.select(2)) decoder_1 (
    .out0(decoder_1_out0), .out1(decoder_1_out1), .out2(decoder_1_out2), .out3(decoder_1_out3),
    .sel(select_reg), .en(in_5));
  Multiplexer #(.select(2), .width(4)) multiplexer_1 (
    .in0(register_1_q), .in1(register_2_q), .in2(register_3_q), .in3(register_4_q), .out(ReadData_1),
    .sel(ReadReg_1));
  Multiplexer #(.select(2), .width(4)) multiplexer_2 (
    .in0(register_1_q), .in1(register_2_q), .in2(register_3_q), .in3(register_4_q), .out(ReadData_2),
    .sel(ReadReg_2));
endmodule

module ALUtest (
  input  [3:0] FromReg_1,
  input  [3:0] FromReg_2,
  input  [1:0] SplitOp
);

  wire [3:0] adder_1_out, multiplexer_1_out, negator_1_out, negator_2_out, subtractor_1_out;

  Adder #(.width(4)) adder_1 (.a(FromReg_1), .b(FromReg_2), .out(adder_1_out));  // open: cin, cout
  Subtractor #(.width(4)) subtractor_1 (.a(FromReg_1), .b(FromReg_2), .out(subtractor_1_out));  // open: bin, bout
  Negator #(.width(4)) negator_1 (.in(FromReg_1), .out(negator_1_out));
  Negator #(.width(4)) negator_2 (.in(FromReg_2), .out(negator_2_out));
  Multiplexer #(.select(2), .width(4)) multiplexer_1 (
    .in0(adder_1_out), .in1(subtractor_1_out), .in2(negator_1_out), .in3(negator_2_out),
    .out(multiplexer_1_out), .sel(SplitOp));
  // Probe on multiplexer_1_out
endmodule
