// Logisim project Programcounter.circ as structural Verilog: 1 circuit, main circuit PC
module PC (
  input  [7:0] in_1,
  input  in_2
);

  wire clock_1_out;
  wire [7:0] counter_1_q;

  Clock clock_1 (.out(clock_1_out));
  Counter counter_1 (.load(in_2), .D(in_1), .Q(counter_1_q), .clk(clock_1_out));  // open: count, carry, up, clr
endmodule
