// Logisim project RegisterFile.circ as structural Verilog: 2 circuits, main circuit main
module main (
);

  RF rf_1 ();  // open: ReadReg_1, ReadReg_2, CLK_enable, Write_data, select_reg_pin, ReadData_1, ReadData_2
endmodule

module RF (
  input  [1:0] ReadReg_1,
  input  [1:0] ReadReg_2,
  input  CLK_enable,
  input  [3:0] Write_data,
  input  [1:0] select_reg_pin,
  output [3:0] ReadData_1,
  output [3:0] ReadData_2
);

  wire and_1_out, and_2_out, and_3_out, and_4_out, decoder_1_out0, decoder_1_out1, decoder_1_out2,
       decoder_1_out3;
  wire [3:0] register_1_q, register_2_q, register_3_q, register_4_q;

  and and_1 (and_1_out, CLK_enable, decoder_1_out0);
  and and_2 (and_2_out, CLK_enable, decoder_1_out1);
  and and_3 (and_3_out, CLK_enable, decoder_1_out2);
  and and_4 (and_4_out, CLK_enable, decoder_1_out3);
  Register #(.width(4)) register_1 (.D(Write_data), .Q(register_1_q), .clk(and_1_out));  // open: en, clr
  Register #(.width(4)) register_2 (.D(Write_data), .Q(register_2_q), .clk(and_2_out));  // open: en, clr
  Register #(.width(4)) register_3 (.D(Write_data), .Q(register_3_q), .clk(and_3_out));  // open: en, clr
  Register #(.width(4)) register_4 (.D(Write_data), .Q(register_4_q), .clk(and_4_out));  // open: en, clr
  Decoder #(.select(2)) decoder_1 (
    .out0(decoder_1_out0), .out1(decoder_1_out1), .out2(decoder_1_out2), .out3(decoder_1_out3),
    .sel(select_reg_pin), .en(CLK_enable));
  Multiplexer #(.select(2), .width(4)) multiplexer_1 (
    .in0(register_1_q), .in1(register_2_q), .in2(register_3_q), .in3(register_4_q), .out(ReadData_1),
    .sel(ReadReg_1));
  Multiplexer #(.select(2), .width(4)) multiplexer_2 (
    .in0(register_1_q), .in1(register_2_q), .in2(register_3_q), .in3(register_4_q), .out(ReadData_2),
    .sel(ReadReg_2));
endmodule
